// Logisim project sumador_con_mux.circ as structural Verilog: 1 circuit, main circuit main
module main (
  input  C,
  input  S0,
  input  S1,
  input  z,
  input  y,
  input  x,
  output S,
  output C_2,
  output S_2,
  output C_3
);

  wire half_adder_1_out_3, half_adder_1_out_4, half_adder_2_out_4, not_1_out;

  not not_1 (not_1_out, z);
  Half_Adder half_adder_1 (.in_1(S0), .in_2(S1), .out_3(half_adder_1_out_3), .out_4(half_adder_1_out_4));
  Multiplexer #(.select(2)) multiplexer_1 (
    .in0(z), .in1(not_1_out), .in2(not_1_out), .in3(z), .out(S_2), .sel({y, x}), .en(1'b1));
  Half_Adder half_adder_2 (.in_1(C), .in_2(half_adder_1_out_3), .out_3(S), .out_4(half_adder_2_out_4));
  or or_1 (C_2, half_adder_2_out_4, half_adder_1_out_4);
  Multiplexer #(.select(2)) multiplexer_2 (
    .in0(1'b0), .in1(z), .in2(z), .in3(1'b1), .out(C_3), .sel({y, x}), .en(1'b1));
endmodule
